# Fritzing sketch bidirectional-motor (saved by Fritzing 0.9.0b)
breadboards: 1

parts:
  Part1 = Spark Core (v1.0)
  D1 = Rectifier Diode [part_number=1N4001 package="Melf DO-213 AB [SMD]"]
  D2 = Rectifier Diode [part_number=1N4001 package="Melf DO-213 AB [SMD]"]
  VCC1 = 4 x AAA Battery Mount
  IC1 = L293D [package=THT]
  D4 = Rectifier Diode [part_number=1N4001 package="Melf DO-213 AB [SMD]"]
  D5 = Rectifier Diode [part_number=1N4001 package="Melf DO-213 AB [SMD]"]
  D6 = Rectifier Diode [part_number=1N4001 package="Melf DO-213 AB [SMD]"]
  D7 = Rectifier Diode [part_number=1N4001 package="Melf DO-213 AB [SMD]"]
  D8 = Rectifier Diode [part_number=1N4001 package="Melf DO-213 AB [SMD]"]
  M1 = DC Motor
  C5 = Electrolytic Capacitor [capacitance=100μF package="100 mil [THT, electrolytic]"]
  M2 = DC Motor
  D3 = Rectifier Diode [part_number=1N4001 package="Melf DO-213 AB [SMD]"]

nets:
  N1: Part1.A0, IC1.Enable_1
  N2: Part1.A1, IC1.Enable_2
  N3: Part1.GND, VCC1.-, IC1.0V, D4.anode, D5.anode, D6.anode, C5.-, D3.anode
  N4: Part1.VIN, D1.cathode, D2.cathode, VCC1.+, IC1.+Vmotor, IC1.+V, D7.cathode, D8.cathode, C5.+
  N5: Part1.D2, IC1.In_4
  N6: Part1.D3, IC1.In_3
  N7: Part1.D4, IC1.In_2
  N8: Part1.D5, IC1.In_1
  N9: D1.anode, IC1.Out_4_(_Controlled_by_Enable_2_), D4.cathode, M2.pin_1
  N10: D2.anode, IC1.Out_3_(_Controlled_by_Enable_2_), M2.pin_2, D3.cathode
  N11: IC1.Out_1_(_Controlled_by_Enable_1_), D6.cathode, D8.anode, M1.pin_2
  N12: IC1.Out_2_(_Controlled_by_Enable_1_), D5.cathode, D7.anode, M1.pin_1
