# Fritzing sketch motor-controller (saved by Fritzing 0.9.0b)
breadboards: 1

parts:
  Part1 = Spark Core (v1.0)
  IC1 = L293D [package=THT]
  D1 = Rectifier Diode [part_number=1N4001 package="Melf DO-213 AB [SMD]"]
  D2 = Rectifier Diode [part_number=1N4001 package="Melf DO-213 AB [SMD]"]
  VCC1 = 4 x AAA Battery Mount
  C6 = Electrolytic Capacitor [capacitance=100μF package="100 mil [THT, electrolytic]"]
  LED1 = LED - 5mm [color="White (4500K)" package="5 mm [THT]"]
  LED2 = LED - 5mm [color="White (4500K)" package="5 mm [THT]"]

nets:
  N1: Part1.A0, IC1.In_4
  N2: Part1.A1, IC1.In_3
  N3: Part1.GND, IC1.0V, D1.anode, D2.anode, VCC1.-, C6.-, LED1.cathode, LED2.cathode
  N4: Part1.VIN, IC1.+Vmotor, IC1.Enable_2, IC1.+V, VCC1.+, C6.+
  N5: IC1.Out_3_(_Controlled_by_Enable_2_), D2.cathode, LED1.anode
  N6: IC1.Out_4_(_Controlled_by_Enable_2_), D1.cathode, LED2.anode
