# Fritzing sketch motors (saved by Fritzing 0.9.0b)
breadboards: 1

parts:
  Part1 = Spark Core (v1.0)
  IC1 = L293D [package=THT]
  D1 = Rectifier Diode [part_number=1N4001 package="Melf DO-213 AB [SMD]"]
  D2 = Rectifier Diode [part_number=1N4001 package="Melf DO-213 AB [SMD]"]
  M1 = DC Motor
  VCC1 = 4 x AAA Battery Mount
  M2 = DC Motor
  C6 = Electrolytic Capacitor [capacitance=100μF package="100 mil [THT, electrolytic]"]
  J2 = Basic Servo

nets:
  N1: Part1.A1, J2.pulse
  N2: Part1.A6, IC1.In_4
  N3: Part1.A7, IC1.In_3
  GND: Part1.GND, IC1.0V, D1.anode, D2.anode, M1.pin_1, VCC1.-, M2.pin_2, C6.-, J2.gnd
  VIN: Part1.VIN, IC1.+Vmotor, IC1.Enable_2, IC1.+V, VCC1.+, C6.+, J2.vcc
  N4: IC1.Out_3_(_Controlled_by_Enable_2_), D2.cathode, M2.pin_1
  N5: IC1.Out_4_(_Controlled_by_Enable_2_), D1.cathode, M1.pin_2
