# Fritzing sketch nodeboats (saved by Fritzing 0.9.0b)
breadboards: 1

parts:
  Part1 = Spark Core (v1.0)
  IC1 = L293D [package=THT]
  D1 = Rectifier Diode [part_number=1N4001 package="Melf DO-213 AB [SMD]"]
  D2 = Rectifier Diode [part_number=1N4001 package="Melf DO-213 AB [SMD]"]
  M1 = DC Motor
  M2 = DC Motor
  VCC1 = 4 x AAA Battery Mount

nets:
  N1: Part1.A6, IC1.In_2
  N2: Part1.A7, IC1.In_1
  N3: Part1.GND, IC1.0V, M1.pin_1, M2.pin_2, VCC1.-
  N4: Part1.VIN, IC1.Enable_1, IC1.+Vmotor, IC1.+V, D1.anode, D2.anode, VCC1.+
  N5: IC1.Out_1_(_Controlled_by_Enable_1_), D2.cathode, M2.pin_1
  N6: IC1.Out_2_(_Controlled_by_Enable_1_), D1.cathode, M1.pin_2
